// Logisim project jk-ff.circ as structural Verilog: 1 circuit, main circuit main
// a
module main (
  input  a,
  input  clock,
  input  b
);

  wire nand_2_out, nand_3_out, nand_4_out, nand_out;

  nand \nand  (nand_out, nand_4_out, a, clock);
  nand nand_2 (nand_2_out, clock, b, nand_3_out);
  nand nand_3 (nand_3_out, nand_out, nand_4_out);
  nand nand_4 (nand_4_out, nand_3_out, nand_2_out);
  LED led_1 (.in(nand_3_out));
  LED led_2 (.in(nand_4_out));

  // Notes on the sheet:
  //   JK-Flip Flop
  //   q
  //   q'
endmodule
