// Logisim project or-gate.circ as structural Verilog: 1 circuit, main circuit main
module main (
  input  in_1,
  input  in_2
);

  wire or_1_out;

  or or_1 (or_1_out, in_1, in_2);
  LED led_1 (.in(or_1_out));

  // Notes on the sheet:
  //   OR gate
  //   a
  //   0
  //   0
  //   1
  //   1
  //   Truth Table for OR-Gate
  //   b
  //   0
  //   1
  //   0
  //   1
  //   y=a+b
  //   0
  //   1
  //   1
  //   1
endmodule
