// Logisim project sr-ff.circ as structural Verilog: 1 circuit, main circuit main
module main (
  input  a,
  input  Clock,
  input  b
);

  wire nand_2_out, nand_3_out, nand_4_out, nand_out;

  nand \nand  (nand_out, a, Clock);
  nand nand_2 (nand_2_out, Clock, b);
  nand nand_3 (nand_3_out, nand_out, nand_4_out);
  nand nand_4 (nand_4_out, nand_3_out, nand_2_out, nand_2_out);
  LED led_1 (.in(nand_3_out));
  LED led_2 (.in(nand_4_out));

  // Notes on the sheet:
  //   SR FLip Flop
  //   clock
  //   a
  //   0
  //   1
  //   0
  //   0
  //   1
  //   1
  //   1
  //   1
  //   1
  //   b
  //   0
  //   0
  //   0
  //   1
  //   0
  //   1
  //   q
  //   q'
  //   q
  //   memory
  //   memory
  //   0
  //   1
  //   not valid
  //   q'
  //   memory
  //   memory
  //   1
  //   0
  //   not valid
endmodule
