// Logisim project xor-gate.circ as structural Verilog: 1 circuit, main circuit main
module main (
  input  a,
  input  b
);

  wire xor_1_out;

  xor xor_1 (xor_1_out, a, b);
  LED led_1 (.in(xor_1_out));

  // Notes on the sheet:
  //   Xor Gate
  //   y
  //   a
  //   0
  //   0
  //   1
  //   1
  //   b
  //   0
  //   1
  //   0
  //   1
  //   0
  //   1
  //   1
  //   0
  //   y
endmodule
